// Logisim project 3_bit_up_counter.circ as structural Verilog: 1 circuit, main circuit main
module main (
  input  in_1,
  input  in_2
);

  wire clock_1_out, j_k_ff_1_q, j_k_ff_1_qn, j_k_ff_2_q, j_k_ff_2_qn, j_k_ff_3_q;

  J_K_Flip_Flop j_k_ff_1 (
    .J(in_1), .K(in_2), .clk(clock_1_out), .Q(j_k_ff_1_q), .Qn(j_k_ff_1_qn), .preset(1'b0), .reset(1'b0));
  Clock clock_1 (.out(clock_1_out));
  LED led_1 (.in(j_k_ff_1_q));
  LED led_2 (.in(j_k_ff_2_q));
  J_K_Flip_Flop j_k_ff_2 (
    .J(in_1), .K(in_2), .clk(j_k_ff_1_qn), .Q(j_k_ff_2_q), .Qn(j_k_ff_2_qn), .preset(1'b0), .reset(1'b0));
  LED led_3 (.in(j_k_ff_3_q));
  J_K_Flip_Flop j_k_ff_3 (
    .J(in_1), .K(in_2), .clk(j_k_ff_2_qn), .Q(j_k_ff_3_q), .preset(1'b0), .reset(1'b0));  // open: Qn
endmodule
