// Logisim project json_counter_4_bit.circ as structural Verilog: 1 circuit, main circuit main
module main (
);

  wire clock_1_out, d_ff_1_q, d_ff_2_q, d_ff_3_q, d_ff_4_q, d_ff_4_qn;

  Clock clock_1 (.out(clock_1_out));
  D_Flip_Flop d_ff_1 (.D(d_ff_4_qn), .clk(clock_1_out), .Q(d_ff_1_q), .preset(1'b0), .reset(1'b0));  // open: Qn
  LED led_1 (.in(d_ff_1_q));
  D_Flip_Flop d_ff_2 (.D(d_ff_1_q), .clk(clock_1_out), .Q(d_ff_2_q), .preset(1'b0), .reset(1'b0));  // open: Qn
  LED led_2 (.in(d_ff_2_q));
  LED led_3 (.in(d_ff_3_q));
  LED led_4 (.in(d_ff_4_q));
  D_Flip_Flop d_ff_3 (.D(d_ff_2_q), .clk(clock_1_out), .Q(d_ff_3_q), .preset(1'b0), .reset(1'b0));  // open: Qn
  D_Flip_Flop d_ff_4 (.D(d_ff_3_q), .clk(clock_1_out), .Q(d_ff_4_q), .Qn(d_ff_4_qn), .preset(1'b0), .reset(1'b0));

  // Notes on the sheet:
  //   johnson counter
endmodule
