// Logisim project ring_counter_4_bit_dff.circ as structural Verilog: 1 circuit, main circuit main
module main (
  input  in_1,
  input  in_2,
  input  in_3
);

  wire and_1_out, clock_1_out, clock_2_out, d_ff_1_q, d_ff_2_q, d_ff_3_q, d_ff_4_q, d_ff_5_q, d_ff_6_q,
       d_ff_7_q, d_ff_8_q, multiplexer_1_out, multiplexer_2_out, nor_1_out, nor_2_out;

  Multiplexer multiplexer_1 (.in0(d_ff_6_q), .in1(in_1), .out(multiplexer_1_out), .sel(in_2));
  nor nor_1 (nor_1_out, d_ff_8_q, d_ff_7_q);
  nor nor_2 (nor_2_out, d_ff_5_q, d_ff_2_q);
  D_Flip_Flop d_ff_1 (.D(multiplexer_1_out), .clk(clock_1_out), .Q(d_ff_1_q), .preset(1'b0), .reset(1'b0));  // open: Qn
  Clock clock_1 (.out(clock_1_out));
  and and_1 (and_1_out, nor_1_out, nor_2_out);
  Multiplexer multiplexer_2 (.in0(d_ff_8_q), .in1(in_3), .out(multiplexer_2_out), .sel(and_1_out));
  LED led_1 (.in(d_ff_1_q));
  D_Flip_Flop d_ff_2 (.D(multiplexer_2_out), .clk(clock_2_out), .Q(d_ff_2_q), .preset(1'b0), .reset(1'b0));  // open: Qn
  Clock clock_2 (.out(clock_2_out));
  LED led_2 (.in(d_ff_3_q));
  D_Flip_Flop d_ff_3 (.D(d_ff_1_q), .clk(clock_1_out), .Q(d_ff_3_q), .preset(1'b0), .reset(1'b0));  // open: Qn
  LED led_3 (.in(d_ff_2_q));
  LED led_4 (.in(d_ff_4_q));
  D_Flip_Flop d_ff_4 (.D(d_ff_3_q), .clk(clock_1_out), .Q(d_ff_4_q), .preset(1'b0), .reset(1'b0));  // open: Qn
  LED led_5 (.in(d_ff_5_q));
  D_Flip_Flop d_ff_5 (.D(d_ff_2_q), .clk(clock_2_out), .Q(d_ff_5_q), .preset(1'b0), .reset(1'b0));  // open: Qn
  LED led_6 (.in(d_ff_6_q));
  D_Flip_Flop d_ff_6 (.D(d_ff_4_q), .clk(clock_1_out), .Q(d_ff_6_q), .preset(1'b0), .reset(1'b0));  // open: Qn
  LED led_7 (.in(d_ff_7_q));
  D_Flip_Flop d_ff_7 (.D(d_ff_5_q), .clk(clock_2_out), .Q(d_ff_7_q), .preset(1'b0), .reset(1'b0));  // open: Qn
  LED led_8 (.in(d_ff_8_q));
  D_Flip_Flop d_ff_8 (.D(d_ff_7_q), .clk(clock_2_out), .Q(d_ff_8_q), .preset(1'b0), .reset(1'b0));  // open: Qn
endmodule
